# Fritzing sketch Arduino Uno Project (saved by Fritzing 0.7.12b)

parts:
  Arduino1 = Arduino
  R1 = Basic Flex Resistor
  R2 = Basic Flex Resistor
  R3 = Basic Flex Resistor
  R4 = Basic Flex Resistor
  R5 = Basic Flex Resistor
  R6 = 22k Ω Resistor [package=THT]
  R7 = 22k Ω Resistor [package=THT]
  R8 = 22k Ω Resistor [package=THT]
  R9 = 22k Ω Resistor [package=THT]
  R10 = 22k Ω Resistor [package=THT]

nets:
  N1: Arduino1.+5V, R1.pin_1, R2.pin_1, R3.pin_1, R4.pin_1, R5.pin_1
  N2: Arduino1.GND, R6.Pin_0, R7.Pin_0, R8.Pin_0, R9.Pin_0, R10.Pin_0
  N3: Arduino1.A0, R1.Pin_2, R6.Pin_1
  N4: Arduino1.A1, R2.Pin_2, R7.Pin_1
  N5: Arduino1.A2, R3.Pin_2, R8.Pin_1
  N6: Arduino1.A3, R4.Pin_2, R9.Pin_1
  N7: Arduino1.A4, R5.Pin_2, R10.Pin_1

notes:
  Thumb
  Index
  Finger
  Middle Finger
  Ring Finger
  Little Finger
